// Logisim project Lab4_GatedDLatch.circ as structural Verilog: 1 circuit, main circuit main
module main (
  input  D,
  input  Clock,
  output Q,
  output nQ
);

  wire c1_p1, c2_p2, c2_p3, c2_p4, c2_p5, c2_p6, c2_p8;

  // _7404 c2: pin names not known; wires that end beside it: D, c2_p2, c2_p3, c2_p4, c2_p5, c2_p6, Q, c2_p8, nQ
  // _7408 c1: pin names not known; wires that end beside it: c1_p1, D, Clock, c2_p3, Clock, c2_p2, c2_p5, c2_p4, nQ, c2_p6, Q, c1_p1, c2_p8
endmodule
